// Logisim project lab10.circ as structural Verilog: 4 circuits, main circuit main
module main (
);

  wire clock_1_out, decoder_1_setmux, fields_1_register, not_1_out;
  wire [1:0] decoder_1_alu;
  wire [3:0] fields_1_opcode;
  wire [7:0] A_q, adder_1_out, ALU_result, B_q, fields_1_immediate, multiplexer_1_out, PC_q;
  wire [15:0] rom_1_data;

  ROM #(.dataWidth(16)) rom_1 (.addr(PC_q), .data(rom_1_data), .sel(1'b1));
  not not_1 (not_1_out, fields_1_register);
  Adder adder_1 (.a(PC_q), .b(8'h1), .out(adder_1_out));  // open: cin, cout
  Register A (.D(multiplexer_1_out), .en(not_1_out), .Q(A_q), .clk(clock_1_out));  // open: clr
  Register B (.D(multiplexer_1_out), .en(fields_1_register), .Q(B_q), .clk(clock_1_out));  // open: clr
  Fields fields_1 (
    .Field_input(rom_1_data), .Immediate(fields_1_immediate), .Register(fields_1_register),
    .Opcode(fields_1_opcode));
  Clock clock_1 (.out(clock_1_out));
  Register PC (.D(adder_1_out), .en(1'b1), .Q(PC_q), .clk(clock_1_out));  // open: clr
  ALU ALU (
    .a(A_q), .b(B_q), .Operation(decoder_1_alu), .Result(ALU_result));  // open: Ainvert, Binvert, CarryIn, CarryOut
  Multiplexer #(.width(8)) multiplexer_1 (
    .in0(ALU_result), .in1(fields_1_immediate), .out(multiplexer_1_out), .sel(decoder_1_setmux));  // open: en
  Decoder decoder_1 (.Opcode(fields_1_opcode), .ALU(decoder_1_alu), .SetMux(decoder_1_setmux));

  // Notes on the sheet:
  //   contents of rom_1 (hex, n*v repeats v):
  //   3 802 2800 3000
  //   SetMux
endmodule

module ALU (
  input  Ainvert,
  input  Binvert,
  input  CarryIn,
  input  [1:0] Operation,
  input  [7:0] a,
  input  [7:0] b,
  output [7:0] Result,
  output CarryOut
);

  wire [7:0] adder_1_out, and_1_out, multiplexer_1_out, multiplexer_2_out, not_1_out, not_2_out, or_1_out,
       subtractor_1_out;

  assign not_1_out = ~a;  // NOT_Gate not_1, 8 bits wide
  assign not_2_out = ~b;  // NOT_Gate not_2, 8 bits wide
  Multiplexer #(.width(8)) multiplexer_1 (
    .in0(a), .in1(not_1_out), .out(multiplexer_1_out), .sel(Ainvert));  // open: en
  Multiplexer #(.width(8)) multiplexer_2 (
    .in0(b), .in1(not_2_out), .out(multiplexer_2_out), .sel(Binvert));  // open: en
  assign and_1_out = multiplexer_1_out & multiplexer_2_out;  // AND_Gate and_1, 8 bits wide
  assign or_1_out = multiplexer_1_out | multiplexer_2_out;  // OR_Gate or_1, 8 bits wide
  Adder adder_1 (.a(multiplexer_1_out), .b(multiplexer_2_out), .out(adder_1_out), .cin(CarryIn), .cout(CarryOut));
  Subtractor subtractor_1 (.a(multiplexer_1_out), .b(multiplexer_2_out), .out(subtractor_1_out));  // open: bin, bout
  Multiplexer #(.select(2), .width(8)) multiplexer_3 (
    .in0(adder_1_out), .in1(subtractor_1_out), .in2(or_1_out), .in3(and_1_out), .out(Result), .sel(Operation));  // open: en
endmodule

module Fields (
  input  [15:0] Field_input,
  output [7:0] Immediate,
  output Register,
  output [3:0] Opcode
);


  assign Immediate = Field_input[7:0];
  assign Opcode = Field_input[15:12];
  assign Register = Field_input[11];
endmodule

module Decoder (
  input  [3:0] Opcode,
  output [1:0] ALU,
  output SetMux
);

  wire not_2_out, not_3_out;

  not not_1 (ALU[0], Opcode[1]);
  not not_2 (not_2_out, Opcode[3]);
  and and_1 (SetMux, not_2_out, not_3_out);
  not not_3 (not_3_out, Opcode[1]);

  assign ALU[1] = Opcode[0];
endmodule
