// Logisim project lab06part2.circ as structural Verilog: 1 circuit, main circuit main
module main (
  input  [7:0] in_1,
  input  [7:0] in_2,
  input  Operation,
  output [7:0] out_4
);

  wire [7:0] adder_1_out, subtractor_1_out;

  Adder adder_1 (.a(in_1), .b(in_2), .out(adder_1_out), .cin(1'b0));  // open: cout
  Subtractor subtractor_1 (.a(in_1), .b(in_2), .out(subtractor_1_out), .bin(1'b0));  // open: bout
  // Probe on adder_1_out
  // Probe on subtractor_1_out
  Multiplexer #(.width(8), .enable("false")) multiplexer_1 (
    .in0(adder_1_out), .in1(subtractor_1_out), .out(out_4), .sel(Operation));

  // Notes on the sheet:
  //   A
  //   B
  //   Result
endmodule
