// Logisim project lab08.circ as structural Verilog: 3 circuits, main circuit main
module main (
  input  [3:0] in_1,
  input  [7:0] a,
  input  [7:0] b,
  output [7:0] out_4,
  output out_5,
  output out_6
);

  _8_bit_ALU u_8_bit_alu_1 (.a(a), .b(b), .ALU_Operation_Code(in_1), .Result(out_4), .Zero(out_5), .Overflow(out_6));
endmodule

module _1_bit_ALU (
  input  Ainvert,
  input  Binvert,
  input  CarryIn,
  input  [1:0] Operation,
  input  a,
  input  b,
  input  Less,
  output Result,
  output CarryOut,
  output Set
);

  wire and_1_out, multiplexer_1_out, multiplexer_2_out, not_1_out, not_2_out, or_1_out;

  not not_1 (not_1_out, a);
  not not_2 (not_2_out, b);
  Multiplexer multiplexer_1 (.in0(a), .in1(not_1_out), .out(multiplexer_1_out), .sel(Ainvert));  // open: en
  Multiplexer multiplexer_2 (.in0(b), .in1(not_2_out), .out(multiplexer_2_out), .sel(Binvert));  // open: en
  and and_1 (and_1_out, multiplexer_1_out, multiplexer_2_out);
  or or_1 (or_1_out, multiplexer_1_out, multiplexer_2_out);
  Adder #(.width(1)) adder_1 (.a(multiplexer_1_out), .b(multiplexer_2_out), .out(Set), .cin(CarryIn), .cout(CarryOut));
  Multiplexer #(.select(2)) multiplexer_3 (
    .in0(and_1_out), .in1(or_1_out), .in2(Set), .in3(Less), .out(Result), .sel(Operation));  // open: en
endmodule

module _8_bit_ALU (
  input  [3:0] ALU_Operation_Code,
  input  [7:0] a,
  input  [7:0] b,
  output [7:0] Result,
  output Zero,
  output Overflow
);

  wire n1_bit_alu_1_carryout, n1_bit_alu_2_carryout, n1_bit_alu_3_carryout, n1_bit_alu_4_carryout,
       n1_bit_alu_5_carryout, n1_bit_alu_6_carryout, n1_bit_alu_7_carryout, n1_bit_alu_8_set, or_1_out;

  _1_bit_ALU u_1_bit_alu_1 (
    .a(a[0]), .b(b[0]), .Less(n1_bit_alu_8_set), .Ainvert(ALU_Operation_Code[3]),
    .Binvert(ALU_Operation_Code[2]), .CarryIn(ALU_Operation_Code[2]), .Operation(ALU_Operation_Code[1:0]),
    .CarryOut(n1_bit_alu_1_carryout), .Result(Result[0]));  // open: Set
  _1_bit_ALU u_1_bit_alu_2 (
    .a(a[1]), .b(b[1]), .Less(1'b0), .Ainvert(ALU_Operation_Code[3]), .Binvert(ALU_Operation_Code[2]),
    .CarryIn(n1_bit_alu_1_carryout), .Operation(ALU_Operation_Code[1:0]), .CarryOut(n1_bit_alu_2_carryout),
    .Result(Result[1]));  // open: Set
  _1_bit_ALU u_1_bit_alu_3 (
    .a(a[2]), .b(b[2]), .Less(1'b0), .Ainvert(ALU_Operation_Code[3]), .Binvert(ALU_Operation_Code[2]),
    .CarryIn(n1_bit_alu_2_carryout), .Operation(ALU_Operation_Code[1:0]), .CarryOut(n1_bit_alu_3_carryout),
    .Result(Result[2]));  // open: Set
  _1_bit_ALU u_1_bit_alu_4 (
    .a(a[3]), .b(b[3]), .Less(1'b0), .Ainvert(ALU_Operation_Code[3]), .Binvert(ALU_Operation_Code[2]),
    .CarryIn(n1_bit_alu_3_carryout), .Operation(ALU_Operation_Code[1:0]), .CarryOut(n1_bit_alu_4_carryout),
    .Result(Result[3]));  // open: Set
  _1_bit_ALU u_1_bit_alu_5 (
    .a(a[4]), .b(b[4]), .Less(1'b0), .Ainvert(ALU_Operation_Code[3]), .Binvert(ALU_Operation_Code[2]),
    .CarryIn(n1_bit_alu_4_carryout), .Operation(ALU_Operation_Code[1:0]), .CarryOut(n1_bit_alu_5_carryout),
    .Result(Result[4]));  // open: Set
  _1_bit_ALU u_1_bit_alu_6 (
    .a(a[5]), .b(b[5]), .Less(1'b0), .Ainvert(ALU_Operation_Code[3]), .Binvert(ALU_Operation_Code[2]),
    .CarryIn(n1_bit_alu_5_carryout), .Operation(ALU_Operation_Code[1:0]), .CarryOut(n1_bit_alu_6_carryout),
    .Result(Result[5]));  // open: Set
  _1_bit_ALU u_1_bit_alu_7 (
    .a(a[6]), .b(b[6]), .Less(1'b0), .Ainvert(ALU_Operation_Code[3]), .Binvert(ALU_Operation_Code[2]),
    .CarryIn(n1_bit_alu_6_carryout), .Operation(ALU_Operation_Code[1:0]), .CarryOut(n1_bit_alu_7_carryout),
    .Result(Result[6]));  // open: Set
  _1_bit_ALU u_1_bit_alu_8 (
    .a(a[7]), .b(b[7]), .Less(1'b0), .Ainvert(ALU_Operation_Code[3]), .Binvert(ALU_Operation_Code[2]),
    .CarryIn(n1_bit_alu_7_carryout), .Operation(ALU_Operation_Code[1:0]), .CarryOut(Overflow),
    .Result(Result[7]), .Set(n1_bit_alu_8_set));
  or or_1 (or_1_out, Result[0], Result[1], Result[2], Result[3], Result[4], Result[5], Result[6], Result[7]);
  not not_1 (Zero, or_1_out);
endmodule
