// Logisim project lab09.circ as structural Verilog: 1 circuit, main circuit main
module main (
  input  writeEnable,
  input  [2:0] Read_Register_1,
  input  [2:0] Read_Register_2,
  input  [2:0] Write_Register,
  input  [31:0] Write_Data,
  input  Clock,
  output [31:0] Read_Data_1,
  output [31:0] Read_Data_2
);

  wire and_1_out, and_2_out, and_3_out, and_4_out, and_5_out, and_6_out, and_7_out, and_8_out,
       decoder_1_out0, decoder_1_out1, decoder_1_out2, decoder_1_out3, decoder_1_out4, decoder_1_out5,
       decoder_1_out6, decoder_1_out7;
  wire [31:0] Register_0_q, Register_1_q, Register_2_q, Register_3_q, Register_4_q, Register_5_q,
       Register_6_q, Register_7_q;

  Decoder #(.select(3)) decoder_1 (
    .out0(decoder_1_out0), .out1(decoder_1_out1), .out2(decoder_1_out2), .out3(decoder_1_out3),
    .out4(decoder_1_out4), .out5(decoder_1_out5), .out6(decoder_1_out6), .out7(decoder_1_out7),
    .sel(Write_Register));  // open: en
  and and_1 (and_1_out, writeEnable, decoder_1_out0);
  and and_2 (and_2_out, writeEnable, decoder_1_out1);
  and and_3 (and_3_out, writeEnable, decoder_1_out2);
  and and_4 (and_4_out, writeEnable, decoder_1_out3);
  and and_5 (and_5_out, writeEnable, decoder_1_out4);
  and and_6 (and_6_out, writeEnable, decoder_1_out5);
  and and_7 (and_7_out, writeEnable, decoder_1_out6);
  and and_8 (and_8_out, writeEnable, decoder_1_out7);
  Register #(.width(32)) Register_0 (.D(Write_Data), .en(and_1_out), .Q(Register_0_q), .clk(Clock));  // open: clr
  Register #(.width(32)) Register_1 (.D(Write_Data), .en(and_2_out), .Q(Register_1_q), .clk(Clock));  // open: clr
  Register #(.width(32)) Register_2 (.D(Write_Data), .en(and_3_out), .Q(Register_2_q), .clk(Clock));  // open: clr
  Register #(.width(32)) Register_3 (.D(Write_Data), .en(and_4_out), .Q(Register_3_q), .clk(Clock));  // open: clr
  Register #(.width(32)) Register_4 (.D(Write_Data), .en(and_5_out), .Q(Register_4_q), .clk(Clock));  // open: clr
  Register #(.width(32)) Register_5 (.D(Write_Data), .en(and_6_out), .Q(Register_5_q), .clk(Clock));  // open: clr
  Register #(.width(32)) Register_6 (.D(Write_Data), .en(and_7_out), .Q(Register_6_q), .clk(Clock));  // open: clr
  Register #(.width(32)) Register_7 (.D(Write_Data), .en(and_8_out), .Q(Register_7_q), .clk(Clock));  // open: clr
  Multiplexer #(.select(3), .width(32)) multiplexer_1 (
    .in0(Register_0_q), .in1(Register_1_q), .in2(Register_2_q), .in3(Register_3_q), .in4(Register_4_q),
    .in5(Register_5_q), .in6(Register_6_q), .in7(Register_7_q), .out(Read_Data_1), .sel(Read_Register_1));  // open: en
  Multiplexer #(.select(3), .width(32)) multiplexer_2 (
    .in0(Register_0_q), .in1(Register_1_q), .in2(Register_2_q), .in3(Register_3_q), .in4(Register_4_q),
    .in5(Register_5_q), .in6(Register_6_q), .in7(Register_7_q), .out(Read_Data_2), .sel(Read_Register_2));  // open: en
endmodule
