// Logisim project 32bitALU.circ as structural Verilog: 3 circuits, main circuit main
module main (
  input  [3:0] in_1,
  input  [31:0] a,
  input  [31:0] b,
  output out_4,
  output [31:0] out_5,
  output out_6
);

  _32_bit_ALU u_32_bit_alu_1 (.a(a), .b(b), .ALU_Operation_Code(in_1), .Zero(out_4), .Result(out_5), .Overflow(out_6));
endmodule

module _1_bit_ALU (
  input  Ainvert,
  input  Binvert,
  input  CarryIn,
  input  [1:0] Operation,
  input  a,
  input  b,
  input  Less,
  output Result,
  output CarryOut,
  output Set
);

  wire and_1_out, multiplexer_1_out, multiplexer_2_out, not_1_out, not_2_out, or_1_out;

  not not_1 (not_1_out, a);
  not not_2 (not_2_out, b);
  Multiplexer multiplexer_1 (.in0(a), .in1(not_1_out), .out(multiplexer_1_out), .sel(Ainvert));  // open: en
  Multiplexer multiplexer_2 (.in0(b), .in1(not_2_out), .out(multiplexer_2_out), .sel(Binvert));  // open: en
  and and_1 (and_1_out, multiplexer_1_out, multiplexer_2_out);
  or or_1 (or_1_out, multiplexer_1_out, multiplexer_2_out);
  Adder #(.width(1)) adder_1 (.a(multiplexer_1_out), .b(multiplexer_2_out), .out(Set), .cin(CarryIn), .cout(CarryOut));
  Multiplexer #(.select(2)) multiplexer_3 (
    .in0(and_1_out), .in1(or_1_out), .in2(Set), .in3(Less), .out(Result), .sel(Operation));  // open: en
endmodule

module _32_bit_ALU (
  input  [3:0] ALU_Operation_Code,
  input  [31:0] a,
  input  [31:0] b,
  output Zero,
  output [31:0] Result,
  output Overflow
);

  wire n1_bit_alu_1_carryout, n1_bit_alu_2_carryout, n1_bit_alu_3_carryout, n1_bit_alu_4_carryout,
       n1_bit_alu_5_carryout, n1_bit_alu_6_carryout, n1_bit_alu_7_carryout, n1_bit_alu_8_carryout,
       n1_bit_alu_9_carryout, n1_bit_alu_10_carryout, n1_bit_alu_11_carryout, n1_bit_alu_12_carryout,
       n1_bit_alu_13_carryout, n1_bit_alu_14_carryout, n1_bit_alu_15_carryout, n1_bit_alu_16_carryout,
       n1_bit_alu_17_carryout, n1_bit_alu_18_carryout, n1_bit_alu_19_carryout, n1_bit_alu_20_carryout,
       n1_bit_alu_21_carryout, n1_bit_alu_22_carryout, n1_bit_alu_23_carryout, n1_bit_alu_24_carryout,
       n1_bit_alu_25_carryout, n1_bit_alu_26_carryout, n1_bit_alu_27_carryout, n1_bit_alu_28_carryout,
       n1_bit_alu_29_carryout, n1_bit_alu_30_carryout, n1_bit_alu_31_carryout, n1_bit_alu_32_set, or_1_out,
       or_2_out, or_3_out, or_4_out, or_5_out, xor_1_out;

  xor xor_1 (xor_1_out, Result[31], Overflow);
  _1_bit_ALU u_1_bit_alu_1 (
    .a(a[0]), .b(b[0]), .Less(n1_bit_alu_32_set), .Ainvert(ALU_Operation_Code[3]),
    .Binvert(ALU_Operation_Code[2]), .CarryIn(ALU_Operation_Code[2]), .Operation(ALU_Operation_Code[1:0]),
    .CarryOut(n1_bit_alu_1_carryout), .Result(Result[0]));  // open: Set
  _1_bit_ALU u_1_bit_alu_2 (
    .a(a[1]), .b(b[1]), .Less(1'b0), .Ainvert(ALU_Operation_Code[3]), .Binvert(ALU_Operation_Code[2]),
    .CarryIn(n1_bit_alu_1_carryout), .Operation(ALU_Operation_Code[1:0]), .CarryOut(n1_bit_alu_2_carryout),
    .Result(Result[1]));  // open: Set
  _1_bit_ALU u_1_bit_alu_3 (
    .a(a[2]), .b(b[2]), .Less(1'b0), .Ainvert(ALU_Operation_Code[3]), .Binvert(ALU_Operation_Code[2]),
    .CarryIn(n1_bit_alu_2_carryout), .Operation(ALU_Operation_Code[1:0]), .CarryOut(n1_bit_alu_3_carryout),
    .Result(Result[2]));  // open: Set
  _1_bit_ALU u_1_bit_alu_4 (
    .a(a[3]), .b(b[3]), .Less(1'b0), .Ainvert(ALU_Operation_Code[3]), .Binvert(ALU_Operation_Code[2]),
    .CarryIn(n1_bit_alu_3_carryout), .Operation(ALU_Operation_Code[1:0]), .CarryOut(n1_bit_alu_4_carryout),
    .Result(Result[3]));  // open: Set
  _1_bit_ALU u_1_bit_alu_5 (
    .a(a[4]), .b(b[4]), .Less(1'b0), .Ainvert(ALU_Operation_Code[3]), .Binvert(ALU_Operation_Code[2]),
    .CarryIn(n1_bit_alu_4_carryout), .Operation(ALU_Operation_Code[1:0]), .CarryOut(n1_bit_alu_5_carryout),
    .Result(Result[4]));  // open: Set
  _1_bit_ALU u_1_bit_alu_6 (
    .a(a[5]), .b(b[5]), .Less(1'b0), .Ainvert(ALU_Operation_Code[3]), .Binvert(ALU_Operation_Code[2]),
    .CarryIn(n1_bit_alu_5_carryout), .Operation(ALU_Operation_Code[1:0]), .CarryOut(n1_bit_alu_6_carryout),
    .Result(Result[5]));  // open: Set
  _1_bit_ALU u_1_bit_alu_7 (
    .a(a[6]), .b(b[6]), .Less(1'b0), .Ainvert(ALU_Operation_Code[3]), .Binvert(ALU_Operation_Code[2]),
    .CarryIn(n1_bit_alu_6_carryout), .Operation(ALU_Operation_Code[1:0]), .CarryOut(n1_bit_alu_7_carryout),
    .Result(Result[6]));  // open: Set
  _1_bit_ALU u_1_bit_alu_8 (
    .a(a[7]), .b(b[7]), .Less(1'b0), .Ainvert(ALU_Operation_Code[3]), .Binvert(ALU_Operation_Code[2]),
    .CarryIn(n1_bit_alu_7_carryout), .Operation(ALU_Operation_Code[1:0]), .CarryOut(n1_bit_alu_8_carryout),
    .Result(Result[7]));  // open: Set
  _1_bit_ALU u_1_bit_alu_9 (
    .a(a[8]), .b(b[8]), .Less(1'b0), .Ainvert(ALU_Operation_Code[3]), .Binvert(ALU_Operation_Code[2]),
    .CarryIn(n1_bit_alu_8_carryout), .Operation(ALU_Operation_Code[1:0]), .CarryOut(n1_bit_alu_9_carryout),
    .Result(Result[8]));  // open: Set
  _1_bit_ALU u_1_bit_alu_10 (
    .a(a[9]), .b(b[9]), .Less(1'b0), .Ainvert(ALU_Operation_Code[3]), .Binvert(ALU_Operation_Code[2]),
    .CarryIn(n1_bit_alu_9_carryout), .Operation(ALU_Operation_Code[1:0]), .CarryOut(n1_bit_alu_10_carryout),
    .Result(Result[9]));  // open: Set
  _1_bit_ALU u_1_bit_alu_11 (
    .a(a[10]), .b(b[10]), .Less(1'b0), .Ainvert(ALU_Operation_Code[3]), .Binvert(ALU_Operation_Code[2]),
    .CarryIn(n1_bit_alu_10_carryout), .Operation(ALU_Operation_Code[1:0]), .CarryOut(n1_bit_alu_11_carryout),
    .Result(Result[10]));  // open: Set
  _1_bit_ALU u_1_bit_alu_12 (
    .a(a[11]), .b(b[11]), .Less(1'b0), .Ainvert(ALU_Operation_Code[3]), .Binvert(ALU_Operation_Code[2]),
    .CarryIn(n1_bit_alu_11_carryout), .Operation(ALU_Operation_Code[1:0]), .CarryOut(n1_bit_alu_12_carryout),
    .Result(Result[11]));  // open: Set
  _1_bit_ALU u_1_bit_alu_13 (
    .a(a[12]), .b(b[12]), .Less(1'b0), .Ainvert(ALU_Operation_Code[3]), .Binvert(ALU_Operation_Code[2]),
    .CarryIn(n1_bit_alu_12_carryout), .Operation(ALU_Operation_Code[1:0]), .CarryOut(n1_bit_alu_13_carryout),
    .Result(Result[12]));  // open: Set
  _1_bit_ALU u_1_bit_alu_14 (
    .a(a[13]), .b(b[13]), .Less(1'b0), .Ainvert(ALU_Operation_Code[3]), .Binvert(ALU_Operation_Code[2]),
    .CarryIn(n1_bit_alu_13_carryout), .Operation(ALU_Operation_Code[1:0]), .CarryOut(n1_bit_alu_14_carryout),
    .Result(Result[13]));  // open: Set
  _1_bit_ALU u_1_bit_alu_15 (
    .a(a[14]), .b(b[14]), .Less(1'b0), .Ainvert(ALU_Operation_Code[3]), .Binvert(ALU_Operation_Code[2]),
    .CarryIn(n1_bit_alu_14_carryout), .Operation(ALU_Operation_Code[1:0]), .CarryOut(n1_bit_alu_15_carryout),
    .Result(Result[14]));  // open: Set
  _1_bit_ALU u_1_bit_alu_16 (
    .a(a[15]), .b(b[15]), .Less(1'b0), .Ainvert(ALU_Operation_Code[3]), .Binvert(ALU_Operation_Code[2]),
    .CarryIn(n1_bit_alu_15_carryout), .Operation(ALU_Operation_Code[1:0]), .CarryOut(n1_bit_alu_16_carryout),
    .Result(Result[15]));  // open: Set
  _1_bit_ALU u_1_bit_alu_17 (
    .a(a[16]), .b(b[16]), .Less(1'b0), .Ainvert(ALU_Operation_Code[3]), .Binvert(ALU_Operation_Code[2]),
    .CarryIn(n1_bit_alu_16_carryout), .Operation(ALU_Operation_Code[1:0]), .CarryOut(n1_bit_alu_17_carryout),
    .Result(Result[16]));  // open: Set
  _1_bit_ALU u_1_bit_alu_18 (
    .a(a[17]), .b(b[17]), .Less(1'b0), .Ainvert(ALU_Operation_Code[3]), .Binvert(ALU_Operation_Code[2]),
    .CarryIn(n1_bit_alu_17_carryout), .Operation(ALU_Operation_Code[1:0]), .CarryOut(n1_bit_alu_18_carryout),
    .Result(Result[17]));  // open: Set
  _1_bit_ALU u_1_bit_alu_19 (
    .a(a[18]), .b(b[18]), .Less(1'b0), .Ainvert(ALU_Operation_Code[3]), .Binvert(ALU_Operation_Code[2]),
    .CarryIn(n1_bit_alu_18_carryout), .Operation(ALU_Operation_Code[1:0]), .CarryOut(n1_bit_alu_19_carryout),
    .Result(Result[18]));  // open: Set
  _1_bit_ALU u_1_bit_alu_20 (
    .a(a[19]), .b(b[19]), .Less(1'b0), .Ainvert(ALU_Operation_Code[3]), .Binvert(ALU_Operation_Code[2]),
    .CarryIn(n1_bit_alu_19_carryout), .Operation(ALU_Operation_Code[1:0]), .CarryOut(n1_bit_alu_20_carryout),
    .Result(Result[19]));  // open: Set
  _1_bit_ALU u_1_bit_alu_21 (
    .a(a[20]), .b(b[20]), .Less(1'b0), .Ainvert(ALU_Operation_Code[3]), .Binvert(ALU_Operation_Code[2]),
    .CarryIn(n1_bit_alu_20_carryout), .Operation(ALU_Operation_Code[1:0]), .CarryOut(n1_bit_alu_21_carryout),
    .Result(Result[20]));  // open: Set
  _1_bit_ALU u_1_bit_alu_22 (
    .a(a[21]), .b(b[21]), .Less(1'b0), .Ainvert(ALU_Operation_Code[3]), .Binvert(ALU_Operation_Code[2]),
    .CarryIn(n1_bit_alu_21_carryout), .Operation(ALU_Operation_Code[1:0]), .CarryOut(n1_bit_alu_22_carryout),
    .Result(Result[21]));  // open: Set
  _1_bit_ALU u_1_bit_alu_23 (
    .a(a[22]), .b(b[22]), .Less(1'b0), .Ainvert(ALU_Operation_Code[3]), .Binvert(ALU_Operation_Code[2]),
    .CarryIn(n1_bit_alu_22_carryout), .Operation(ALU_Operation_Code[1:0]), .CarryOut(n1_bit_alu_23_carryout),
    .Result(Result[22]));  // open: Set
  _1_bit_ALU u_1_bit_alu_24 (
    .a(a[23]), .b(b[23]), .Less(1'b0), .Ainvert(ALU_Operation_Code[3]), .Binvert(ALU_Operation_Code[2]),
    .CarryIn(n1_bit_alu_23_carryout), .Operation(ALU_Operation_Code[1:0]), .CarryOut(n1_bit_alu_24_carryout),
    .Result(Result[23]));  // open: Set
  _1_bit_ALU u_1_bit_alu_25 (
    .a(a[24]), .b(b[24]), .Less(1'b0), .Ainvert(ALU_Operation_Code[3]), .Binvert(ALU_Operation_Code[2]),
    .CarryIn(n1_bit_alu_24_carryout), .Operation(ALU_Operation_Code[1:0]), .CarryOut(n1_bit_alu_25_carryout),
    .Result(Result[24]));  // open: Set
  _1_bit_ALU u_1_bit_alu_26 (
    .a(a[25]), .b(b[25]), .Less(1'b0), .Ainvert(ALU_Operation_Code[3]), .Binvert(ALU_Operation_Code[2]),
    .CarryIn(n1_bit_alu_25_carryout), .Operation(ALU_Operation_Code[1:0]), .CarryOut(n1_bit_alu_26_carryout),
    .Result(Result[25]));  // open: Set
  _1_bit_ALU u_1_bit_alu_27 (
    .a(a[26]), .b(b[26]), .Less(1'b0), .Ainvert(ALU_Operation_Code[3]), .Binvert(ALU_Operation_Code[2]),
    .CarryIn(n1_bit_alu_26_carryout), .Operation(ALU_Operation_Code[1:0]), .CarryOut(n1_bit_alu_27_carryout),
    .Result(Result[26]));  // open: Set
  _1_bit_ALU u_1_bit_alu_28 (
    .a(a[27]), .b(b[27]), .Less(1'b0), .Ainvert(ALU_Operation_Code[3]), .Binvert(ALU_Operation_Code[2]),
    .CarryIn(n1_bit_alu_27_carryout), .Operation(ALU_Operation_Code[1:0]), .CarryOut(n1_bit_alu_28_carryout),
    .Result(Result[27]));  // open: Set
  _1_bit_ALU u_1_bit_alu_29 (
    .a(a[28]), .b(b[28]), .Less(1'b0), .Ainvert(ALU_Operation_Code[3]), .Binvert(ALU_Operation_Code[2]),
    .CarryIn(n1_bit_alu_28_carryout), .Operation(ALU_Operation_Code[1:0]), .CarryOut(n1_bit_alu_29_carryout),
    .Result(Result[28]));  // open: Set
  _1_bit_ALU u_1_bit_alu_30 (
    .a(a[29]), .b(b[29]), .Less(1'b0), .Ainvert(ALU_Operation_Code[3]), .Binvert(ALU_Operation_Code[2]),
    .CarryIn(n1_bit_alu_29_carryout), .Operation(ALU_Operation_Code[1:0]), .CarryOut(n1_bit_alu_30_carryout),
    .Result(Result[29]));  // open: Set
  _1_bit_ALU u_1_bit_alu_31 (
    .a(a[30]), .b(b[30]), .Less(1'b0), .Ainvert(ALU_Operation_Code[3]), .Binvert(ALU_Operation_Code[2]),
    .CarryIn(n1_bit_alu_30_carryout), .Operation(ALU_Operation_Code[1:0]), .CarryOut(n1_bit_alu_31_carryout),
    .Result(Result[30]));  // open: Set
  _1_bit_ALU u_1_bit_alu_32 (
    .a(a[31]), .b(b[31]), .Less(1'b0), .Ainvert(ALU_Operation_Code[3]), .Binvert(ALU_Operation_Code[2]),
    .CarryIn(n1_bit_alu_31_carryout), .Operation(ALU_Operation_Code[1:0]), .CarryOut(Overflow),
    .Result(Result[31]), .Set(n1_bit_alu_32_set));
  or or_1 (or_1_out, Result[0], Result[1], Result[2], Result[3], Result[4], Result[5], Result[6], Result[7]);
  or or_2 (or_2_out, Result[8], Result[9], Result[10], Result[11], Result[12], Result[13], Result[14], Result[15]);
  or or_3 (or_3_out, Result[16], Result[17], Result[18], Result[19], Result[20], Result[21], Result[22], Result[23]);
  or or_4 (or_4_out, Result[24], Result[25], Result[26], Result[27], Result[28], Result[29], Result[30], Result[31]);
  or or_5 (or_5_out, or_1_out, or_2_out, or_3_out, or_4_out);
  not not_1 (Zero, or_5_out);
endmodule
