// Logisim project ledDisplay.circ as structural Verilog: 22 circuits, main circuit main
module main (
);

  wire alu_done_1_set_less_than, clock_1_out, cpu_control_done_1_alusrc, cpu_control_done_1_jump,
       cpu_control_done_1_jump_and_link, cpu_control_done_1_jump_register,
       cpu_control_done_1_load_upper_immediate, cpu_control_done_1_memread, cpu_control_done_1_memtoreg,
       cpu_control_done_1_memwrite, cpu_control_done_1_not, cpu_control_done_1_regdst,
       cpu_control_done_1_regwrite, cpu_control_done_1_shift, cpu_control_done_1_shift_direction,
       cpu_control_done_1_shift_value, cpu_control_done_1_zero_extend, equality_1_equal, not_1_out, or_1_out;
  wire [1:0] cpu_control_done_1_alu_operation, cpu_control_done_1_beq;
  wire [2:0] cpu_control_done_1_byte;
  wire [3:2] cpu_control_done_1_bnegate;
  wire [4:0] fields_1_rd, fields_1_rs, fields_1_rt, fields_1_shamt, multiplexer_1_out, multiplexer_3_out,
       multiplexer_5_out, shamt_and_1_output;
  wire [5:0] fields_1_function, fields_1_opcode;
  wire [7:0] main_memory_1__000, main_memory_1__000_2, main_memory_1__000_3, main_memory_1__000_4;
  wire [15:0] fields_1_immediate, PC_q_2;
  wire [25:0] fields_1_target_address;
  wire [31:0] adder_1_out, alu_done_1_result, jump_control_1_output__ra, jump_control_1_output_pc,
       main_memory_1__001, main_memory_1__010, main_memory_1__011, main_memory_1__100, main_memory_1__101,
       main_memory_1__110, main_memory_1__111, main_memory_1_data, multiplexer_2_out, multiplexer_4_out,
       multiplexer_6_out, multiplexer_7_out, multiplexer_8_out, PC_q, register_file_done_1_read_data_1,
       register_file_done_1_read_data_2, rom_1_data, sign_or_zero_extend_1_output,
       zero_extend_26_to_32_1_result;

  Register #(.width(32), .trigger("falling")) PC (
    .D(jump_control_1_output_pc), .en(1'b1), .Q({PC_q[31:18], PC_q_2, PC_q[1:0]}), .clk(clock_1_out));  // open: clr
  Adder #(.width(32)) adder_1 (.a({PC_q[31:18], PC_q_2, PC_q[1:0]}), .b(32'h4), .out(adder_1_out));  // open: cin, cout
  ROM #(.addrWidth(16), .dataWidth(32)) rom_1 (.addr(PC_q_2), .data(rom_1_data));  // open: sel
  Fields fields_1 (
    .Instruction(rom_1_data), .Opcode(fields_1_opcode), .Function(fields_1_function), .rs(fields_1_rs),
    .rt(fields_1_rt), .rd(fields_1_rd), .shamt(fields_1_shamt), .Immediate(fields_1_immediate),
    .Target_Address(fields_1_target_address));
  CPU_Control__DONE cpu_control_done_1 (
    .Opcode(fields_1_opcode), .Function_field(fields_1_function), .RegDst(cpu_control_done_1_regdst),
    .Jump_Register(cpu_control_done_1_jump_register), .Jump_and_Link(cpu_control_done_1_jump_and_link),
    .Jump(cpu_control_done_1_jump), .BEQ(cpu_control_done_1_beq[0]), .BNE(cpu_control_done_1_beq[1]),
    .MemRead(cpu_control_done_1_memread), .MemToReg(cpu_control_done_1_memtoreg),
    .Ainvert(cpu_control_done_1_bnegate[3]), .Bnegate(cpu_control_done_1_bnegate[2]),
    .ALU_Operation(cpu_control_done_1_alu_operation), .MemWrite(cpu_control_done_1_memwrite),
    .ALUSrc(cpu_control_done_1_alusrc), .RegWrite(cpu_control_done_1_regwrite),
    .Shift(cpu_control_done_1_shift), .Shift_Direction(cpu_control_done_1_shift_direction),
    .Shift_Value(cpu_control_done_1_shift_value), .Byte(cpu_control_done_1_byte[0]),
    .Half(cpu_control_done_1_byte[1]), .Word(cpu_control_done_1_byte[2]),
    .Load_Upper_Immediate(cpu_control_done_1_load_upper_immediate), .NOT(cpu_control_done_1_not),
    .Zero_Extend(cpu_control_done_1_zero_extend));
  Multiplexer #(.width(5)) multiplexer_1 (
    .in0(fields_1_rt), .in1(fields_1_rd), .out(multiplexer_1_out), .sel(cpu_control_done_1_regdst));  // open: en
  not not_1 (not_1_out, cpu_control_done_1_jump_and_link);
  Multiplexer #(.width(32)) multiplexer_2 (
    .in0(adder_1_out), .in1(multiplexer_8_out), .out(multiplexer_2_out), .sel(not_1_out));  // open: en
  Zero_Extend_26_to_32 zero_extend_26_to_32_1 (.Input(fields_1_target_address), .Result(zero_extend_26_to_32_1_result));
  or or_1 (or_1_out, cpu_control_done_1_regwrite, cpu_control_done_1_jump_and_link);
  Multiplexer #(.width(5)) multiplexer_3 (
    .in0(multiplexer_1_out), .in1({5{1'b1}}), .out(multiplexer_3_out), .sel(cpu_control_done_1_jump_and_link));  // open: en
  Register_File__DONE register_file_done_1 (
    .Read_Register_1(fields_1_rs), .Read_Register_2(fields_1_rt), .Write_Register(multiplexer_3_out),
    .Write_Data(multiplexer_2_out), .Write_Enable(or_1_out), .Clock(clock_1_out),
    .Read_Data_1(register_file_done_1_read_data_1), .Read_Data_2(register_file_done_1_read_data_2));
  Sign_or_Zero_Extend sign_or_zero_extend_1 (
    .Input(fields_1_immediate), .Sign__0__or_Zero___shift__1(cpu_control_done_1_load_upper_immediate),
    .Zero_Extend(cpu_control_done_1_zero_extend), .Output(sign_or_zero_extend_1_output));
  Multiplexer #(.width(32)) multiplexer_4 (
    .in0(register_file_done_1_read_data_2), .in1(sign_or_zero_extend_1_output), .out(multiplexer_4_out),
    .sel(cpu_control_done_1_alusrc));  // open: en
  Equality equality_1 (
    .A(register_file_done_1_read_data_1), .Input(register_file_done_1_read_data_2), .Equal(equality_1_equal));
  SHAMT_AND shamt_and_1 (.Input(register_file_done_1_read_data_1), .Output(shamt_and_1_output));
  Multiplexer #(.width(5)) multiplexer_5 (
    .in0(shamt_and_1_output), .in1(fields_1_shamt), .out(multiplexer_5_out),
    .sel(cpu_control_done_1_shift_value));  // open: en
  DotMatrix #(.matrixcols(8), .matrixrows(8), .dotshape("circle")) dotmatrix_1 (
    .col0(main_memory_1__111[31:24]), .col1(main_memory_1__111[23:16]), .col2(main_memory_1__111[15:8]),
    .col3(main_memory_1__111[7:0]), .col4(main_memory_1__110[31:24]), .col5(main_memory_1__110[23:16]),
    .col6(main_memory_1__110[15:8]), .col7(main_memory_1__110[7:0]));
  ALU__DONE alu_done_1 (
    .A(register_file_done_1_read_data_1), .B(multiplexer_4_out), .Shift_amount(multiplexer_5_out),
    .Result(alu_done_1_result), .Operation({cpu_control_done_1_bnegate, cpu_control_done_1_alu_operation}),
    .Shift_Direction(cpu_control_done_1_shift_direction), .Shift(cpu_control_done_1_shift),
    .NOT(cpu_control_done_1_not), .Set_Less_Than(alu_done_1_set_less_than));  // open: Zero
  DotMatrix #(.matrixcols(8), .matrixrows(8), .dotshape("circle")) dotmatrix_2 (
    .col0(main_memory_1__101[31:24]), .col1(main_memory_1__101[23:16]), .col2(main_memory_1__101[15:8]),
    .col3(main_memory_1__101[7:0]), .col4(main_memory_1__100[31:24]), .col5(main_memory_1__100[23:16]),
    .col6(main_memory_1__100[15:8]), .col7(main_memory_1__100[7:0]));
  DotMatrix #(.matrixcols(8), .matrixrows(8), .dotshape("circle")) dotmatrix_3 (
    .col0(main_memory_1__011[31:24]), .col1(main_memory_1__011[23:16]), .col2(main_memory_1__011[15:8]),
    .col3(main_memory_1__011[7:0]), .col4(main_memory_1__010[31:24]), .col5(main_memory_1__010[23:16]),
    .col6(main_memory_1__010[15:8]), .col7(main_memory_1__010[7:0]));
  Jump_Control jump_control_1 (
    .Address(zero_extend_26_to_32_1_result), .Input_PC(adder_1_out), .rs(register_file_done_1_read_data_2),
    .Input__ra(alu_done_1_result), .Immediate(sign_or_zero_extend_1_output), .BNE(cpu_control_done_1_beq[1]),
    .BEQ(cpu_control_done_1_beq[0]), .Jump(cpu_control_done_1_jump),
    .Jump_and_Link(cpu_control_done_1_jump_and_link), .Jump_Register(cpu_control_done_1_jump_register),
    .Equals(equality_1_equal), .Output_PC(jump_control_1_output_pc), .Output__ra(jump_control_1_output__ra));
  DotMatrix #(.matrixcols(8), .matrixrows(8), .dotshape("circle")) dotmatrix_4 (
    .col0(main_memory_1__001[31:24]), .col1(main_memory_1__001[23:16]), .col2(main_memory_1__001[15:8]),
    .col3(main_memory_1__001[7:0]), .col4(main_memory_1__000_4), .col5(main_memory_1__000_3),
    .col6(main_memory_1__000_2), .col7(main_memory_1__000));
  Clock clock_1 (.out(clock_1_out));
  Multiplexer #(.width(32)) multiplexer_6 (
    .in0(jump_control_1_output__ra), .in1(multiplexer_7_out), .out(multiplexer_6_out),
    .sel(cpu_control_done_1_bnegate[3]));  // open: en
  Main_Memory main_memory_1 (
    .Address(multiplexer_6_out), .DataToWrite(register_file_done_1_read_data_2),
    .\byte (cpu_control_done_1_byte[0]), .half(cpu_control_done_1_byte[1]),
    .word(cpu_control_done_1_byte[2]), .MemWrite(cpu_control_done_1_memwrite), ._111(main_memory_1__111),
    ._110(main_memory_1__110), ._101(main_memory_1__101), ._100(main_memory_1__100),
    ._011(main_memory_1__011), ._010(main_memory_1__010), ._001(main_memory_1__001),
    ._000({main_memory_1__000_4, main_memory_1__000_3, main_memory_1__000_2, main_memory_1__000}),
    .clock(clock_1_out), .MemRead(cpu_control_done_1_memread), .Data(main_memory_1_data));
  Multiplexer #(.width(32)) multiplexer_7 (
    .in0({32{1'b0}}), .in1(32'h1), .out(multiplexer_7_out), .sel(alu_done_1_set_less_than));  // open: en
  Multiplexer #(.width(32)) multiplexer_8 (
    .in0(multiplexer_6_out), .in1(main_memory_1_data), .out(multiplexer_8_out),
    .sel(cpu_control_done_1_memtoreg));  // open: en

  // Notes on the sheet:
  //   contents of rom_1 (hex, n*v repeats v):
  //   3c1d7fff 37bdeffc 3c111001 36310120 92320000 12400004 122020 c10000b 22310001 8100004 810000a
  //   23bdfff4 afb10008 afb00004 afbf0000 20100020 1604000d 2020 c100040 2020 c100040 2020 c100040 2020
  //   c100040 2020 c100040 2020 c100040 810003b 2010003a 90802a 12000004 2090ffd0 3c111001 363100d0
  //   8100027 2090ffbf 3c111001 1080c0 2308820 8e300000 102600 42602 c100040 102400 42602 c100040 102200
  //   42602 c100040 102602 c100040 8e300004 102600 42602 c100040 2020 c100040 8fb10008 8fb00004 8fbf0000
  //   23bd000c 3e00008 44020 3c09ffff 35298000 200a0007 1140000a a5880 12b5820 8d6c0000 8d6dfffc c6200
  //   d6e02 18d6025 ad6c0000 214affff 8100044 8d2a0000 a5200 1485025 ad2a0000 3e00008
endmodule

module _8_Word_Direct_Output (
  input  MemWrite,
  input  [31:0] Address,
  input  [31:0] DataIn,
  input  Clock,
  output [31:0] _000,
  output [31:0] _001,
  output [31:0] _010,
  output [31:0] _011,
  output [31:0] _100,
  output [31:0] _101,
  output [31:0] _110,
  output [31:0] _111,
  output [31:0] DataOut
);

  wire and_1_out, and_2_out, and_3_out, and_4_out, and_5_out, and_6_out, and_7_out, and_8_out,
       decoder_1_out0, decoder_1_out1, decoder_1_out2, decoder_1_out3, decoder_1_out4, decoder_1_out5,
       decoder_1_out6, decoder_1_out7;

  Decoder #(.select(3)) decoder_1 (
    .out0(decoder_1_out0), .out1(decoder_1_out1), .out2(decoder_1_out2), .out3(decoder_1_out3),
    .out4(decoder_1_out4), .out5(decoder_1_out5), .out6(decoder_1_out6), .out7(decoder_1_out7),
    .sel(Address[4:2]));  // open: en
  and and_1 (and_1_out, MemWrite, decoder_1_out0);
  and and_2 (and_2_out, MemWrite, decoder_1_out1);
  and and_3 (and_3_out, MemWrite, decoder_1_out2);
  and and_4 (and_4_out, MemWrite, decoder_1_out3);
  and and_5 (and_5_out, MemWrite, decoder_1_out4);
  and and_6 (and_6_out, MemWrite, decoder_1_out5);
  and and_7 (and_7_out, MemWrite, decoder_1_out6);
  and and_8 (and_8_out, MemWrite, decoder_1_out7);
  Register #(.width(32), .trigger("falling")) register_1 (
    .D(DataIn), .en(and_1_out), .Q(_000), .clk(Clock));  // open: clr
  Register #(.width(32), .trigger("falling")) register_2 (
    .D(DataIn), .en(and_2_out), .Q(_001), .clk(Clock));  // open: clr
  Register #(.width(32), .trigger("falling")) register_3 (
    .D(DataIn), .en(and_3_out), .Q(_010), .clk(Clock));  // open: clr
  Register #(.width(32), .trigger("falling")) register_4 (
    .D(DataIn), .en(and_4_out), .Q(_011), .clk(Clock));  // open: clr
  Register #(.width(32), .trigger("falling")) register_5 (
    .D(DataIn), .en(and_5_out), .Q(_100), .clk(Clock));  // open: clr
  Register #(.width(32), .trigger("falling")) register_6 (
    .D(DataIn), .en(and_6_out), .Q(_101), .clk(Clock));  // open: clr
  Register #(.width(32), .trigger("falling")) register_7 (
    .D(DataIn), .en(and_7_out), .Q(_110), .clk(Clock));  // open: clr
  Register #(.width(32), .trigger("falling")) register_8 (
    .D(DataIn), .en(and_8_out), .Q(_111), .clk(Clock));  // open: clr
  Multiplexer #(.select(3), .width(32)) multiplexer_1 (
    .in0(_000), .in1(_001), .in2(_010), .in3(_011), .in4(_100), .in5(_101), .in6(_110), .in7(_111),
    .out(DataOut), .sel(Address[4:2]));  // open: en
endmodule

module Main_Memory (
  input  MemWrite,
  input  [31:0] Address,
  input  [31:0] DataToWrite,
  input  \byte ,
  input  half,
  input  word,
  input  clock,
  input  MemRead,
  output [31:0] _111,
  output [31:0] _110,
  output [31:0] _101,
  output [31:0] _100,
  output [31:0] _011,
  output [31:0] _010,
  output [31:0] _001,
  output [31:0] _000,
  output [31:0] Data
);

  wire address_comparator_1_active, address_comparator_2_active, address_comparator_3_active, and_3_out,
       and_4_out, and_5_out, and_6_out, and_7_out, not_1_out, not_2_out, not_3_out, not_4_out;
  wire [1:0] address_comparator_1_output_address_2, and_2_out;
  wire [7:0] multiplexer_5_out;
  wire [15:0] multiplexer_4_out;
  wire [31:0] address_comparator_2_output_address, address_comparator_3_output_address,
       controlled_buffer_1_out, multiplexer_1_out, multiplexer_2_out, multiplexer_3_out,
       n8_word_direct_output_1_dataout, ram_1_data, ram_2_data;
  wire [31:2] address_comparator_1_output_address;

  Address_Comparator address_comparator_1 (
    .Input_Address(Address), .Starting_Address(32'h10010000), .Memory_Size(32'h4000000), .isStack(1'b0),
    .Active(address_comparator_1_active),
    .Output_Address({address_comparator_1_output_address, address_comparator_1_output_address_2}));
  Address_Comparator address_comparator_2 (
    .Input_Address(Address), .Starting_Address(32'h7fffeffc), .Memory_Size(32'h4000000), .isStack(1'b1),
    .Active(address_comparator_2_active), .Output_Address(address_comparator_2_output_address));
  Address_Comparator address_comparator_3 (
    .Input_Address(Address), .Starting_Address(32'hffff8000), .Memory_Size(32'h20), .isStack(1'b0),
    .Active(address_comparator_3_active), .Output_Address(address_comparator_3_output_address));
  not not_1 (not_1_out, \byte );
  not not_2 (not_2_out, half);
  not not_3 (not_3_out, word);
  and and_1 (and_2_out[1], \byte , not_2_out, not_3_out);
  and and_2 (and_2_out[0], not_1_out, half, not_3_out);
  Multiplexer #(.select(2), .width(32)) multiplexer_1 (
    .in0({controlled_buffer_1_out[31:8], DataToWrite[7:0]}),
    .in1({controlled_buffer_1_out[31:16], DataToWrite[7:0], controlled_buffer_1_out[7:0]}),
    .in2({controlled_buffer_1_out[31:24], DataToWrite[7:0], controlled_buffer_1_out[15:0]}),
    .in3({DataToWrite[7:0], controlled_buffer_1_out[23:0]}), .out(multiplexer_1_out),
    .sel(address_comparator_1_output_address_2));  // open: en
  Multiplexer #(.width(32)) multiplexer_2 (
    .in0({controlled_buffer_1_out[31:16], DataToWrite[15:0]}),
    .in1({DataToWrite[15:0], controlled_buffer_1_out[15:0]}), .out(multiplexer_2_out),
    .sel(address_comparator_1_output_address_2[1]));  // open: en
  Multiplexer #(.select(2), .width(32)) multiplexer_3 (
    .in0(DataToWrite), .in1(multiplexer_2_out), .in2(multiplexer_1_out), .out(multiplexer_3_out),
    .sel(and_2_out));  // open: in3, en
  and and_3 (and_3_out, MemWrite, and_6_out);
  and and_4 (and_4_out, MemWrite, address_comparator_2_active);
  and and_5 (and_5_out, address_comparator_3_active, MemWrite);
  _8_Word_Direct_Output u_8_word_direct_output_1 (
    .Address(address_comparator_3_output_address), .DataIn(multiplexer_3_out), .MemWrite(and_5_out),
    .Clock(clock), ._000(_000), ._001(_001), ._010(_010), ._011(_011), ._100(_100), ._101(_101), ._110(_110),
    ._111(_111), .DataOut(n8_word_direct_output_1_dataout));
  assign controlled_buffer_1_out = address_comparator_3_active ? n8_word_direct_output_1_dataout : 32'bz;  // Controlled_Buffer controlled_buffer_1
  not not_4 (not_4_out, address_comparator_3_active);
  RAM #(.addrWidth(24), .dataWidth(32), .bus("separate")) ram_1 (
    .addr(address_comparator_1_output_address[25:2]), .din(multiplexer_3_out), .data(ram_1_data),
    .str(and_3_out), .clk(clock));  // open: sel, ld, clr
  RAM #(.addrWidth(24), .dataWidth(32), .bus("separate")) ram_2 (
    .addr(address_comparator_2_output_address[25:2]), .din(multiplexer_3_out), .data(ram_2_data),
    .str(and_4_out), .clk(clock));  // open: sel, ld, clr
  assign controlled_buffer_1_out = and_6_out ? ram_1_data : 32'bz;  // Controlled_Buffer controlled_buffer_2
  and and_6 (and_6_out, not_4_out, address_comparator_1_active);
  assign controlled_buffer_1_out = and_7_out ? ram_2_data : 32'bz;  // Controlled_Buffer controlled_buffer_3
  and and_7 (and_7_out, not_4_out, address_comparator_2_active);
  Multiplexer #(.width(16)) multiplexer_4 (
    .in0(controlled_buffer_1_out[15:0]), .in1(controlled_buffer_1_out[31:16]), .out(multiplexer_4_out),
    .sel(address_comparator_1_output_address_2[1]));  // open: en
  Multiplexer #(.select(2), .width(8)) multiplexer_5 (
    .in0(controlled_buffer_1_out[7:0]), .in1(controlled_buffer_1_out[15:8]),
    .in2(controlled_buffer_1_out[23:16]), .in3(controlled_buffer_1_out[31:24]), .out(multiplexer_5_out),
    .sel(address_comparator_1_output_address_2));  // open: en
  Multiplexer #(.select(2), .width(32)) multiplexer_6 (
    .in0(controlled_buffer_1_out), .in1({{16{1'b0}}, multiplexer_4_out}),
    .in2({{24{1'b0}}, multiplexer_5_out}), .in3({32{1'b0}}), .out(Data), .sel(and_2_out), .en(MemRead));
endmodule

module Address_Comparator (
  input  [31:0] Input_Address,
  input  [31:0] Starting_Address,
  input  [31:0] Memory_Size,
  input  isStack,
  output Active,
  output [31:0] Output_Address
);

  wire and_1_out, and_2_out, comparator_1_eq, comparator_1_gt, comparator_2_lt, comparator_3_eq,
       comparator_3_lt, comparator_4_gt, or_1_out, or_2_out;
  wire [31:0] adder_1_out, subtractor_1_out, subtractor_2_out, subtractor_3_out;

  Comparator #(.width(32), .mode("unsigned")) comparator_1 (
    .a(Input_Address), .b(Starting_Address), .gt(comparator_1_gt), .eq(comparator_1_eq));  // open: lt
  Comparator #(.width(32), .mode("unsigned")) comparator_2 (
    .a(Input_Address), .b(adder_1_out), .lt(comparator_2_lt));  // open: gt, eq
  Adder #(.width(32)) adder_1 (.a(Starting_Address), .b(Memory_Size), .out(adder_1_out));  // open: cin, cout
  Subtractor #(.width(32)) subtractor_1 (
    .a(Input_Address), .b(Starting_Address), .out(subtractor_1_out));  // open: bin, bout
  Comparator #(.width(32), .mode("unsigned")) comparator_3 (
    .a(Input_Address), .b(Starting_Address), .eq(comparator_3_eq), .lt(comparator_3_lt));  // open: gt
  Comparator #(.width(32), .mode("unsigned")) comparator_4 (
    .a(Input_Address), .b(subtractor_2_out), .gt(comparator_4_gt));  // open: eq, lt
  Subtractor #(.width(32)) subtractor_2 (
    .a(Starting_Address), .b(Memory_Size), .out(subtractor_2_out));  // open: bin, bout
  Subtractor #(.width(32)) subtractor_3 (
    .a(Starting_Address), .b(Input_Address), .out(subtractor_3_out));  // open: bin, bout
  or or_1 (or_1_out, comparator_1_gt, comparator_1_eq);
  and and_1 (and_1_out, or_1_out, comparator_2_lt);
  or or_2 (or_2_out, comparator_3_eq, comparator_3_lt);
  and and_2 (and_2_out, or_2_out, comparator_4_gt);
  Multiplexer multiplexer_1 (.in0(and_1_out), .in1(and_2_out), .out(Active), .sel(isStack));  // open: en
  Multiplexer #(.width(32)) multiplexer_2 (
    .in0(subtractor_1_out), .in1(subtractor_3_out), .out(Output_Address), .sel(isStack));  // open: en
endmodule

// ALU
module ALU__DONE (
  input  [3:0] Operation,
  input  NOT,
  input  [31:0] A,
  input  [31:0] B,
  input  [4:0] Shift_amount,
  input  Shift_Direction,
  input  Shift,
  output Zero,
  output Set_Less_Than,
  output [31:0] Result
);

  wire [31:0] multiplexer_1_out, multiplexer_2_out, n32_bit_alu_1_result, not_1_out, shifter_1_out,
       shifter_2_out;

  Shifter #(.width(32)) shifter_1 (.in(B), .\dist (Shift_amount), .out(shifter_1_out));
  Shifter #(.width(32), .shift("lr")) shifter_2 (.in(B), .\dist (Shift_amount), .out(shifter_2_out));
  _32_bit_ALU u_32_bit_alu_1 (
    .a(A), .b(B), .ALU_Operation_Code(Operation), .Result(n32_bit_alu_1_result), .Overflow(Set_Less_Than));  // open: Zero
  Multiplexer #(.width(32)) multiplexer_1 (
    .in0(shifter_1_out), .in1(shifter_2_out), .out(multiplexer_1_out), .sel(Shift_Direction));  // open: en
  Multiplexer #(.width(32)) multiplexer_2 (
    .in0(n32_bit_alu_1_result), .in1(multiplexer_1_out), .out(multiplexer_2_out), .sel(Shift));  // open: en
  assign not_1_out = ~multiplexer_2_out;  // NOT_Gate not_1, 32 bits wide
  Multiplexer #(.width(32)) multiplexer_3 (
    .in0(multiplexer_2_out), .in1(not_1_out), .out(Result), .sel(NOT));  // open: en
  CheckZero checkzero_1 (.Input(Result), .Zero(Zero));
endmodule

// Regists
module Register_File__DONE (
  input  Write_Enable,
  input  [4:0] Read_Register_1,
  input  [4:0] Read_Register_2,
  input  [4:0] Write_Register,
  input  [31:0] Write_Data,
  input  Clock,
  output [31:0] Read_Data_1,
  output [31:0] Read_Data_2
);

  wire and_1_out, and_2_out, and_3_out, and_4_out, and_5_out, and_6_out, and_7_out, and_8_out, and_9_out,
       and_10_out, and_11_out, and_12_out, and_13_out, and_14_out, and_15_out, and_16_out, and_17_out,
       and_18_out, and_19_out, and_20_out, and_21_out, and_22_out, and_23_out, and_24_out, and_25_out,
       and_26_out, and_27_out, and_28_out, and_29_out, and_30_out, and_31_out, and_32_out, decoder_1_out0,
       decoder_1_out1, decoder_1_out2, decoder_1_out3, decoder_1_out4, decoder_1_out5, decoder_1_out6,
       decoder_1_out7, decoder_1_out8, decoder_1_out9, decoder_1_out10, decoder_1_out11, decoder_1_out12,
       decoder_1_out13, decoder_1_out14, decoder_1_out15, decoder_1_out16, decoder_1_out17, decoder_1_out18,
       decoder_1_out19, decoder_1_out20, decoder_1_out21, decoder_1_out22, decoder_1_out23, decoder_1_out24,
       decoder_1_out25, decoder_1_out26, decoder_1_out27, decoder_1_out28, decoder_1_out29, decoder_1_out30,
       decoder_1_out31;
  wire [31:0] Register_0_q, Register_1_q, Register_2_q, Register_3_q, Register_4_q, Register_5_q,
       Register_6_q, Register_7_q, Register_8_q, Register_9_q, Register_10_q, Register_11_q, Register_12_q,
       Register_13_q, Register_14_q, Register_15_q, Register_16_q, Register_17_q, Register_18_q,
       Register_19_q, Register_20_q, Register_21_q, Register_22_q, Register_23_q, Register_24_q,
       Register_25_q, Register_26_q, Register_27_q, Register_28_q, Register_29_q, Register_30_q,
       Register_31_q;

  Decoder #(.select(5)) decoder_1 (
    .out0(decoder_1_out0), .out1(decoder_1_out1), .out2(decoder_1_out2), .out3(decoder_1_out3),
    .out4(decoder_1_out4), .out5(decoder_1_out5), .out6(decoder_1_out6), .out7(decoder_1_out7),
    .out8(decoder_1_out8), .out9(decoder_1_out9), .out10(decoder_1_out10), .out11(decoder_1_out11),
    .out12(decoder_1_out12), .out13(decoder_1_out13), .out14(decoder_1_out14), .out15(decoder_1_out15),
    .out16(decoder_1_out16), .out17(decoder_1_out17), .out18(decoder_1_out18), .out19(decoder_1_out19),
    .out20(decoder_1_out20), .out21(decoder_1_out21), .out22(decoder_1_out22), .out23(decoder_1_out23),
    .out24(decoder_1_out24), .out25(decoder_1_out25), .out26(decoder_1_out26), .out27(decoder_1_out27),
    .out28(decoder_1_out28), .out29(decoder_1_out29), .out30(decoder_1_out30), .out31(decoder_1_out31),
    .sel(Write_Register));  // open: en
  and and_1 (and_1_out, Write_Enable, decoder_1_out0);
  and and_2 (and_2_out, Write_Enable, decoder_1_out1);
  and and_3 (and_3_out, Write_Enable, decoder_1_out2);
  and and_4 (and_4_out, Write_Enable, decoder_1_out3);
  and and_5 (and_5_out, Write_Enable, decoder_1_out4);
  and and_6 (and_6_out, Write_Enable, decoder_1_out5);
  and and_7 (and_7_out, Write_Enable, decoder_1_out6);
  and and_8 (and_8_out, Write_Enable, decoder_1_out7);
  and and_9 (and_9_out, Write_Enable, decoder_1_out8);
  and and_10 (and_10_out, Write_Enable, decoder_1_out9);
  and and_11 (and_11_out, Write_Enable, decoder_1_out10);
  and and_12 (and_12_out, Write_Enable, decoder_1_out11);
  and and_13 (and_13_out, Write_Enable, decoder_1_out12);
  and and_14 (and_14_out, Write_Enable, decoder_1_out13);
  and and_15 (and_15_out, Write_Enable, decoder_1_out14);
  and and_16 (and_16_out, Write_Enable, decoder_1_out15);
  and and_17 (and_17_out, Write_Enable, decoder_1_out16);
  and and_18 (and_18_out, Write_Enable, decoder_1_out17);
  and and_19 (and_19_out, Write_Enable, decoder_1_out18);
  and and_20 (and_20_out, Write_Enable, decoder_1_out19);
  and and_21 (and_21_out, Write_Enable, decoder_1_out20);
  and and_22 (and_22_out, Write_Enable, decoder_1_out21);
  and and_23 (and_23_out, Write_Enable, decoder_1_out22);
  and and_24 (and_24_out, Write_Enable, decoder_1_out23);
  and and_25 (and_25_out, Write_Enable, decoder_1_out24);
  and and_26 (and_26_out, Write_Enable, decoder_1_out25);
  and and_27 (and_27_out, Write_Enable, decoder_1_out26);
  and and_28 (and_28_out, Write_Enable, decoder_1_out27);
  and and_29 (and_29_out, Write_Enable, decoder_1_out28);
  and and_30 (and_30_out, Write_Enable, decoder_1_out29);
  and and_31 (and_31_out, Write_Enable, decoder_1_out30);
  and and_32 (and_32_out, Write_Enable, decoder_1_out31);
  Register #(.width(32)) Register_0 (.D(Write_Data), .en(and_1_out), .Q(Register_0_q), .clk(Clock));  // open: clr
  Register #(.width(32)) Register_1 (.D(Write_Data), .en(and_2_out), .Q(Register_1_q), .clk(Clock));  // open: clr
  Register #(.width(32)) Register_2 (.D(Write_Data), .en(and_3_out), .Q(Register_2_q), .clk(Clock));  // open: clr
  Register #(.width(32)) Register_3 (.D(Write_Data), .en(and_4_out), .Q(Register_3_q), .clk(Clock));  // open: clr
  Register #(.width(32)) Register_4 (.D(Write_Data), .en(and_5_out), .Q(Register_4_q), .clk(Clock));  // open: clr
  Register #(.width(32)) Register_5 (.D(Write_Data), .en(and_6_out), .Q(Register_5_q), .clk(Clock));  // open: clr
  Register #(.width(32)) Register_6 (.D(Write_Data), .en(and_7_out), .Q(Register_6_q), .clk(Clock));  // open: clr
  Register #(.width(32)) Register_7 (.D(Write_Data), .en(and_8_out), .Q(Register_7_q), .clk(Clock));  // open: clr
  Register #(.width(32)) Register_8 (.D(Write_Data), .en(and_9_out), .Q(Register_8_q), .clk(Clock));  // open: clr
  Register #(.width(32)) Register_9 (.D(Write_Data), .en(and_10_out), .Q(Register_9_q), .clk(Clock));  // open: clr
  Register #(.width(32)) Register_10 (.D(Write_Data), .en(and_11_out), .Q(Register_10_q), .clk(Clock));  // open: clr
  Register #(.width(32)) Register_11 (.D(Write_Data), .en(and_12_out), .Q(Register_11_q), .clk(Clock));  // open: clr
  Register #(.width(32)) Register_12 (.D(Write_Data), .en(and_13_out), .Q(Register_12_q), .clk(Clock));  // open: clr
  Register #(.width(32)) Register_13 (.D(Write_Data), .en(and_14_out), .Q(Register_13_q), .clk(Clock));  // open: clr
  Register #(.width(32)) Register_14 (.D(Write_Data), .en(and_15_out), .Q(Register_14_q), .clk(Clock));  // open: clr
  Register #(.width(32)) Register_15 (.D(Write_Data), .en(and_16_out), .Q(Register_15_q), .clk(Clock));  // open: clr
  Register #(.width(32)) Register_16 (.D(Write_Data), .en(and_17_out), .Q(Register_16_q), .clk(Clock));  // open: clr
  Register #(.width(32)) Register_17 (.D(Write_Data), .en(and_18_out), .Q(Register_17_q), .clk(Clock));  // open: clr
  Register #(.width(32)) Register_18 (.D(Write_Data), .en(and_19_out), .Q(Register_18_q), .clk(Clock));  // open: clr
  Register #(.width(32)) Register_19 (.D(Write_Data), .en(and_20_out), .Q(Register_19_q), .clk(Clock));  // open: clr
  Register #(.width(32)) Register_20 (.D(Write_Data), .en(and_21_out), .Q(Register_20_q), .clk(Clock));  // open: clr
  Register #(.width(32)) Register_21 (.D(Write_Data), .en(and_22_out), .Q(Register_21_q), .clk(Clock));  // open: clr
  Register #(.width(32)) Register_22 (.D(Write_Data), .en(and_23_out), .Q(Register_22_q), .clk(Clock));  // open: clr
  Register #(.width(32)) Register_23 (.D(Write_Data), .en(and_24_out), .Q(Register_23_q), .clk(Clock));  // open: clr
  Register #(.width(32)) Register_24 (.D(Write_Data), .en(and_25_out), .Q(Register_24_q), .clk(Clock));  // open: clr
  Register #(.width(32)) Register_25 (.D(Write_Data), .en(and_26_out), .Q(Register_25_q), .clk(Clock));  // open: clr
  Register #(.width(32)) Register_26 (.D(Write_Data), .en(and_27_out), .Q(Register_26_q), .clk(Clock));  // open: clr
  Register #(.width(32)) Register_27 (.D(Write_Data), .en(and_28_out), .Q(Register_27_q), .clk(Clock));  // open: clr
  Register #(.width(32)) Register_28 (.D(Write_Data), .en(and_29_out), .Q(Register_28_q), .clk(Clock));  // open: clr
  Register #(.width(32)) Register_29 (.D(Write_Data), .en(and_30_out), .Q(Register_29_q), .clk(Clock));  // open: clr
  Register #(.width(32)) Register_30 (.D(Write_Data), .en(and_31_out), .Q(Register_30_q), .clk(Clock));  // open: clr
  Register #(.width(32)) Register_31 (.D(Write_Data), .en(and_32_out), .Q(Register_31_q), .clk(Clock));  // open: clr
  Multiplexer #(.select(5), .width(32)) multiplexer_1 (
    .in0(Register_0_q), .in1(Register_1_q), .in2(Register_2_q), .in3(Register_3_q), .in4(Register_4_q),
    .in5(Register_5_q), .in6(Register_6_q), .in7(Register_7_q), .in8(Register_8_q), .in9(Register_9_q),
    .in10(Register_10_q), .in11(Register_11_q), .in12(Register_12_q), .in13(Register_13_q),
    .in14(Register_14_q), .in15(Register_15_q), .in16(Register_16_q), .in17(Register_17_q),
    .in18(Register_18_q), .in19(Register_19_q), .in20(Register_20_q), .in21(Register_21_q),
    .in22(Register_22_q), .in23(Register_23_q), .in24(Register_24_q), .in25(Register_25_q),
    .in26(Register_26_q), .in27(Register_27_q), .in28(Register_28_q), .in29(Register_29_q),
    .in30(Register_30_q), .in31(Register_31_q), .out(Read_Data_1), .sel(Read_Register_1));  // open: en
  Multiplexer #(.select(5), .width(32)) multiplexer_2 (
    .in0(Register_0_q), .in1(Register_1_q), .in2(Register_2_q), .in3(Register_3_q), .in4(Register_4_q),
    .in5(Register_5_q), .in6(Register_6_q), .in7(Register_7_q), .in8(Register_8_q), .in9(Register_9_q),
    .in10(Register_10_q), .in11(Register_11_q), .in12(Register_12_q), .in13(Register_13_q),
    .in14(Register_14_q), .in15(Register_15_q), .in16(Register_16_q), .in17(Register_17_q),
    .in18(Register_18_q), .in19(Register_19_q), .in20(Register_20_q), .in21(Register_21_q),
    .in22(Register_22_q), .in23(Register_23_q), .in24(Register_24_q), .in25(Register_25_q),
    .in26(Register_26_q), .in27(Register_27_q), .in28(Register_28_q), .in29(Register_29_q),
    .in30(Register_30_q), .in31(Register_31_q), .out(Read_Data_2), .sel(Read_Register_2));  // open: en
endmodule

// Sign Extend
module Sign_Extend__DONE (
  input  [15:0] Input,
  output [31:0] Result
);


  assign Result = {{17{Input[15]}}, Input[14:0]};
endmodule

// sll 2
module Shift_Left_2__DONE (
  input  [31:0] Input,
  output [31:0] Result
);

  Shifter #(.width(32)) shifter_1 (.in(Input), .\dist (5'b00010), .out(Result));
endmodule

module Shift_Left_2_Expand__DONE (
  input  [25:0] Input,
  output [27:0] Result
);

  Shifter #(.width(26)) shifter_1 (.in(Input), .\dist (5'b00010), .out(Result[25:0]));

  assign Result[27:26] = Input[25:24];
endmodule

// Zero Extend
module Zero_Extend__DONE (
  input  [15:0] Input,
  output [31:0] Result
);


  assign Result = {{16{1'b0}}, Input};
endmodule

// Control
module CPU_Control__DONE (
  input  [5:0] Opcode,
  input  [5:0] Function_field,
  output RegDst,
  output Jump_Register,
  output Jump_and_Link,
  output Jump,
  output BEQ,
  output BNE,
  output MemRead,
  output MemToReg,
  output Ainvert,
  output Bnegate,
  output [1:0] ALU_Operation,
  output MemWrite,
  output ALUSrc,
  output RegWrite,
  output Shift,
  output Shift_Direction,
  output Shift_Value,
  output Byte,
  output Half,
  output Word,
  output Load_Upper_Immediate,
  output NOT,
  output Zero_Extend
);

  wire add_out, addi_out, ALU_add_out, ALU_or_out, and_out, andi_out, lbu_out, lhu_out, lw_out, not_1_out,
       not_2_out, not_3_out, not_4_out, not_5_out, not_6_out, not_7_out, not_8_out, not_9_out, not_10_out,
       not_11_out, not_12_out, not_13_out, not_14_out, or_2_out, or_3_out, or_4_out, ori_out, R_type_out,
       rd_instructs_out, sb_out, sh_out, sll_out, sllv_out, slt_out, slti_out, srl_out, srlv_out, sw_out;

  not not_1 (not_1_out, Opcode[5]);
  not not_2 (not_2_out, Opcode[4]);
  not not_3 (not_3_out, Opcode[3]);
  not not_4 (not_4_out, Opcode[2]);
  not not_5 (not_5_out, Opcode[0]);
  not not_6 (not_6_out, Opcode[1]);
  and R_type (R_type_out, not_1_out, not_2_out, not_3_out, not_4_out, not_6_out, not_5_out);
  and addi (addi_out, not_1_out, not_2_out, Opcode[3], not_4_out, not_6_out, not_5_out);
  and andi (andi_out, not_1_out, not_2_out, Opcode[3], Opcode[2], not_6_out, not_5_out);
  and ori (ori_out, not_1_out, not_2_out, Opcode[3], Opcode[2], not_6_out, Opcode[0]);
  and slti (slti_out, not_1_out, not_2_out, Opcode[3], not_4_out, Opcode[1], not_5_out);
  and lbu (lbu_out, Opcode[5], not_2_out, not_3_out, Opcode[2], not_6_out, not_5_out);
  and sb (sb_out, Opcode[5], not_2_out, Opcode[3], not_4_out, not_6_out, not_5_out);
  and lhu (lhu_out, Opcode[5], not_2_out, not_3_out, Opcode[2], not_6_out, Opcode[0]);
  and sh (sh_out, Opcode[5], not_2_out, Opcode[3], not_4_out, not_6_out, Opcode[0]);
  and lw (lw_out, Opcode[5], not_2_out, not_3_out, not_4_out, Opcode[1], Opcode[0]);
  and sw (sw_out, Opcode[5], not_2_out, Opcode[3], not_4_out, Opcode[1], Opcode[0]);
  and u_beq (BEQ, not_1_out, not_2_out, not_3_out, Opcode[2], not_6_out, not_5_out);
  and u_bne (BNE, not_1_out, not_2_out, not_3_out, Opcode[2], not_6_out, Opcode[0]);
  and j (Jump, not_1_out, not_2_out, not_3_out, not_4_out, Opcode[1], not_5_out);
  and jal (Jump_and_Link, not_1_out, not_2_out, not_3_out, not_4_out, Opcode[1], Opcode[0]);
  and lui (Load_Upper_Immediate, not_1_out, not_2_out, Opcode[3], Opcode[2], Opcode[1], Opcode[0]);
  or u_Byte (Byte, lbu_out, sb_out);
  or u_Half (Half, lhu_out, sh_out);
  or u_Word (Word, lw_out, sw_out);
  or u_MemRead (MemRead, lbu_out, lhu_out, lw_out);
  or or_1 (Zero_Extend, ori_out, andi_out);
  or u_MemWrite (MemWrite, sb_out, sh_out, sw_out);
  not not_7 (not_7_out, Function_field[4]);
  not not_8 (not_8_out, Function_field[3]);
  not not_9 (not_9_out, Function_field[5]);
  not not_10 (not_10_out, Function_field[2]);
  not not_11 (not_11_out, Function_field[0]);
  not not_12 (not_12_out, Function_field[1]);
  and add (add_out, Function_field[5], not_7_out, not_8_out, R_type_out, not_10_out, not_12_out, not_11_out);
  and \and  (and_out, Function_field[5], not_7_out, not_8_out, R_type_out, Function_field[2], not_12_out, not_11_out);
  and \nor  (NOT, Function_field[5], not_7_out, not_8_out, R_type_out, Function_field[2], Function_field[1], Function_field[0]);
  and or_2 (or_2_out, Function_field[5], not_7_out, not_8_out, R_type_out, Function_field[2], not_12_out, Function_field[0]);
  and slt (slt_out, Function_field[5], not_7_out, Function_field[3], R_type_out, not_10_out, Function_field[1], not_11_out);
  and sll (sll_out, not_9_out, not_7_out, not_8_out, R_type_out, not_10_out, not_12_out, not_11_out);
  and sllv (sllv_out, not_9_out, not_7_out, not_8_out, R_type_out, Function_field[2], not_12_out, not_11_out);
  and srl (srl_out, not_9_out, not_7_out, not_8_out, R_type_out, not_10_out, Function_field[1], not_11_out);
  and srlv (srlv_out, not_9_out, not_7_out, not_8_out, R_type_out, Function_field[2], Function_field[1], not_11_out);
  and sub (Bnegate, Function_field[5], not_7_out, not_8_out, R_type_out, not_10_out, Function_field[1], not_11_out);
  and jr (Jump_Register, not_9_out, not_7_out, Function_field[3], R_type_out, not_10_out, not_12_out, not_11_out);
  or or_3 (or_3_out, BEQ, BNE, Jump, Jump_and_Link);
  // OR_Gate Shift_Left has open pins: in0=sll_out, in1=sllv_out, out=open
  or u_Shift (Shift, sll_out, sllv_out, srl_out, srlv_out);
  or Shift_Right (Shift_Direction, srl_out, srlv_out);
  or shamt_field (Shift_Value, sll_out, srl_out);
  or or_4 (or_4_out, or_3_out, MemWrite);
  // OR_Gate AlU_and has open pins: in0=and_out, in1=andi_out, out=open
  or ALU_or (ALU_or_out, NOT, or_2_out, ori_out);
  or ALU_less (Ainvert, slt_out, slti_out);
  not not_13 (not_13_out, or_4_out);
  or ALU_add (ALU_add_out, add_out, Load_Upper_Immediate, addi_out, Jump_Register, Bnegate, MemRead, MemWrite);
  or or_5 (ALU_Operation[0], ALU_or_out, Ainvert);
  or or_6 (ALU_Operation[1], ALU_add_out, Ainvert);
  or rd_instructs (rd_instructs_out, add_out, and_out, NOT, or_2_out, slt_out, Bnegate);
  or I_type (ALUSrc, addi_out, andi_out, ori_out, slti_out, MemRead, MemWrite, BEQ, BNE, Load_Upper_Immediate);
  not not_14 (not_14_out, Jump_Register);
  or or_7 (RegDst, rd_instructs_out, Shift);
  and and_2 (RegWrite, not_13_out, not_14_out);

  assign MemToReg = MemRead;
endmodule

module CheckZero (
  input  [31:0] Input,
  output Zero
);

  wire or_1_out;

  not not_1 (Zero, or_1_out);
  or or_1 (or_1_out, Input[0], Input[1], Input[2], Input[3], Input[4], Input[5], Input[6], Input[7], Input[8], Input[9], Input[10], Input[11], Input[12], Input[13], Input[14], Input[15], Input[16], Input[17], Input[18], Input[19], Input[20], Input[21], Input[22], Input[23], Input[24], Input[25], Input[26], Input[27], Input[28], Input[29], Input[30], Input[31]);
endmodule

// Equal
module Equality (
  input  [31:0] A,
  input  [31:0] Input,
  output Equal
);

  wire [31:0] xor_1_out;

  assign xor_1_out = A ^ Input;  // XOR_Gate xor_1, 32 bits wide
  CheckZero checkzero_1 (.Input(xor_1_out), .Zero(Equal));
endmodule

module Fields (
  input  [31:0] Instruction,
  output [5:0] Opcode,
  output [5:0] Function,
  output [4:0] rs,
  output [4:0] rt,
  output [4:0] rd,
  output [4:0] shamt,
  output [15:0] Immediate,
  output [25:0] Target_Address
);


  assign Function = Instruction[5:0];
  assign Immediate = Instruction[15:0];
  assign Opcode = Instruction[31:26];
  assign rd = Instruction[15:11];
  assign rs = Instruction[25:21];
  assign rt = Instruction[20:16];
  assign shamt = Instruction[10:6];
  assign Target_Address = Instruction[25:0];
endmodule

module ALU_Control (
  input  Negate,
  input  [15:0] A,
  input  [15:0] B
);
endmodule

// short
module SHAMT_AND (
  input  [31:0] Input,
  output [4:0] Output
);


  assign Output = Input[4:0];
endmodule

module Jump (
  input  [31:0] Address,
  input  [31:0] Input_PC,
  output [31:0] Result_PC
);

  wire [31:0] and_1_out, shifter_1_out;

  Shifter #(.width(32)) shifter_1 (.in(Address), .\dist (5'b00010), .out(shifter_1_out));
  assign and_1_out = Input_PC & 32'hf0000000;  // AND_Gate and_1, 32 bits wide
  assign Result_PC = shifter_1_out | and_1_out;  // OR_Gate or_1, 32 bits wide
endmodule

// 0 Ext
module Zero_Extend_26_to_32 (
  input  [25:0] Input,
  output [31:0] Result
);


  assign Result = {{6{1'b0}}, Input};
endmodule

// Jump Cont
module Jump_Control (
  input  BNE,
  input  BEQ,
  input  Jump,
  input  Jump_and_Link,
  input  Jump_Register,
  input  [31:0] Address,
  input  [31:0] Input_PC,
  input  [31:0] rs,
  input  [31:0] Input__ra,
  input  [31:0] Immediate,
  input  Equals,
  output [31:0] Output_PC,
  output [31:0] Output__ra
);

  wire and_1_out, and_2_out, not_1_out, not_2_out, or_1_out, or_2_out;
  wire [31:0] adder_1_out, j_and_jal_result_pc, multiplexer_1_out, multiplexer_2_out,
       shift_left_2_done_1_result;

  Jump j_and_jal (.Address(Address), .Input_PC(Input_PC), .Result_PC(j_and_jal_result_pc));
  Shift_Left_2__DONE shift_left_2_done_1 (.Input(Immediate), .Result(shift_left_2_done_1_result));
  and and_1 (and_1_out, not_1_out, BNE);
  or or_1 (or_1_out, and_1_out, and_2_out);
  Adder #(.width(32)) adder_1 (.a(Input_PC), .b(shift_left_2_done_1_result), .out(adder_1_out));  // open: cin, cout
  and and_2 (and_2_out, BEQ, Equals);
  not not_1 (not_1_out, Equals);
  Multiplexer #(.width(32)) multiplexer_1 (
    .in0(multiplexer_2_out), .in1(j_and_jal_result_pc), .out(multiplexer_1_out), .sel(or_2_out));  // open: en
  Multiplexer #(.width(32)) multiplexer_2 (
    .in0(Input_PC), .in1(adder_1_out), .out(multiplexer_2_out), .sel(or_1_out));  // open: en
  or or_2 (or_2_out, Jump, Jump_and_Link);
  Multiplexer #(.width(32)) multiplexer_3 (
    .in0(multiplexer_1_out), .in1(Input__ra), .out(Output_PC), .sel(Jump_Register));  // open: en
  Multiplexer #(.width(32)) multiplexer_4 (
    .in0(Input_PC), .in1(Input__ra), .out(Output__ra), .sel(not_2_out));  // open: en
  not not_2 (not_2_out, Jump_and_Link);
endmodule

// Sign or Zero
module Sign_or_Zero_Extend (
  input  Sign__0__or_Zero___shift__1,
  input  Zero_Extend,
  input  [15:0] Input,
  output [31:0] Output
);

  wire [31:0] multiplexer_1_out, shifter_1_out, sign_extend_done_1_result, zero_extend_done_1_result,
       zero_extend_done_2_result;

  Sign_Extend__DONE sign_extend_done_1 (.Input(Input), .Result(sign_extend_done_1_result));
  Zero_Extend__DONE zero_extend_done_1 (.Input(Input), .Result(zero_extend_done_1_result));
  Zero_Extend__DONE zero_extend_done_2 (.Input(Input), .Result(zero_extend_done_2_result));
  Shifter #(.width(32)) shifter_1 (.in(zero_extend_done_1_result), .\dist (5'b10000), .out(shifter_1_out));
  Multiplexer #(.width(32)) multiplexer_1 (
    .in0(sign_extend_done_1_result), .in1(shifter_1_out), .out(multiplexer_1_out),
    .sel(Sign__0__or_Zero___shift__1));  // open: en
  Multiplexer #(.width(32)) multiplexer_2 (
    .in0(multiplexer_1_out), .in1(zero_extend_done_2_result), .out(Output), .sel(Zero_Extend));  // open: en
endmodule

module _1_bit_ALU (
  input  Ainvert,
  input  Binvert,
  input  CarryIn,
  input  [1:0] Operation,
  input  a,
  input  b,
  input  Less,
  output Result,
  output CarryOut,
  output Set
);

  wire and_1_out, multiplexer_1_out, multiplexer_2_out, not_1_out, not_2_out, or_1_out;

  not not_1 (not_1_out, a);
  not not_2 (not_2_out, b);
  Multiplexer multiplexer_1 (.in0(a), .in1(not_1_out), .out(multiplexer_1_out), .sel(Ainvert));  // open: en
  Multiplexer multiplexer_2 (.in0(b), .in1(not_2_out), .out(multiplexer_2_out), .sel(Binvert));  // open: en
  and and_1 (and_1_out, multiplexer_1_out, multiplexer_2_out);
  or or_1 (or_1_out, multiplexer_1_out, multiplexer_2_out);
  Adder #(.width(1)) adder_1 (.a(multiplexer_1_out), .b(multiplexer_2_out), .out(Set), .cin(CarryIn), .cout(CarryOut));
  Multiplexer #(.select(2)) multiplexer_3 (
    .in0(and_1_out), .in1(or_1_out), .in2(Set), .in3(Less), .out(Result), .sel(Operation));  // open: en
endmodule

module _32_bit_ALU (
  input  [3:0] ALU_Operation_Code,
  input  [31:0] a,
  input  [31:0] b,
  output Zero,
  output [31:0] Result,
  output Overflow
);

  wire n1_bit_alu_1_carryout, n1_bit_alu_2_carryout, n1_bit_alu_3_carryout, n1_bit_alu_4_carryout,
       n1_bit_alu_5_carryout, n1_bit_alu_6_carryout, n1_bit_alu_7_carryout, n1_bit_alu_8_carryout,
       n1_bit_alu_9_carryout, n1_bit_alu_10_carryout, n1_bit_alu_11_carryout, n1_bit_alu_12_carryout,
       n1_bit_alu_13_carryout, n1_bit_alu_14_carryout, n1_bit_alu_15_carryout, n1_bit_alu_16_carryout,
       n1_bit_alu_17_carryout, n1_bit_alu_18_carryout, n1_bit_alu_19_carryout, n1_bit_alu_20_carryout,
       n1_bit_alu_21_carryout, n1_bit_alu_22_carryout, n1_bit_alu_23_carryout, n1_bit_alu_24_carryout,
       n1_bit_alu_25_carryout, n1_bit_alu_26_carryout, n1_bit_alu_27_carryout, n1_bit_alu_28_carryout,
       n1_bit_alu_29_carryout, n1_bit_alu_30_carryout, n1_bit_alu_31_carryout, n1_bit_alu_32_set, or_1_out,
       or_2_out, or_3_out, or_4_out, or_5_out, xor_1_out;

  xor xor_1 (xor_1_out, Result[31], Overflow);
  _1_bit_ALU u_1_bit_alu_1 (
    .a(a[0]), .b(b[0]), .Less(n1_bit_alu_32_set), .Ainvert(ALU_Operation_Code[3]),
    .Binvert(ALU_Operation_Code[2]), .CarryIn(ALU_Operation_Code[2]), .Operation(ALU_Operation_Code[1:0]),
    .CarryOut(n1_bit_alu_1_carryout), .Result(Result[0]));  // open: Set
  _1_bit_ALU u_1_bit_alu_2 (
    .a(a[1]), .b(b[1]), .Less(1'b0), .Ainvert(ALU_Operation_Code[3]), .Binvert(ALU_Operation_Code[2]),
    .CarryIn(n1_bit_alu_1_carryout), .Operation(ALU_Operation_Code[1:0]), .CarryOut(n1_bit_alu_2_carryout),
    .Result(Result[1]));  // open: Set
  _1_bit_ALU u_1_bit_alu_3 (
    .a(a[2]), .b(b[2]), .Less(1'b0), .Ainvert(ALU_Operation_Code[3]), .Binvert(ALU_Operation_Code[2]),
    .CarryIn(n1_bit_alu_2_carryout), .Operation(ALU_Operation_Code[1:0]), .CarryOut(n1_bit_alu_3_carryout),
    .Result(Result[2]));  // open: Set
  _1_bit_ALU u_1_bit_alu_4 (
    .a(a[3]), .b(b[3]), .Less(1'b0), .Ainvert(ALU_Operation_Code[3]), .Binvert(ALU_Operation_Code[2]),
    .CarryIn(n1_bit_alu_3_carryout), .Operation(ALU_Operation_Code[1:0]), .CarryOut(n1_bit_alu_4_carryout),
    .Result(Result[3]));  // open: Set
  _1_bit_ALU u_1_bit_alu_5 (
    .a(a[4]), .b(b[4]), .Less(1'b0), .Ainvert(ALU_Operation_Code[3]), .Binvert(ALU_Operation_Code[2]),
    .CarryIn(n1_bit_alu_4_carryout), .Operation(ALU_Operation_Code[1:0]), .CarryOut(n1_bit_alu_5_carryout),
    .Result(Result[4]));  // open: Set
  _1_bit_ALU u_1_bit_alu_6 (
    .a(a[5]), .b(b[5]), .Less(1'b0), .Ainvert(ALU_Operation_Code[3]), .Binvert(ALU_Operation_Code[2]),
    .CarryIn(n1_bit_alu_5_carryout), .Operation(ALU_Operation_Code[1:0]), .CarryOut(n1_bit_alu_6_carryout),
    .Result(Result[5]));  // open: Set
  _1_bit_ALU u_1_bit_alu_7 (
    .a(a[6]), .b(b[6]), .Less(1'b0), .Ainvert(ALU_Operation_Code[3]), .Binvert(ALU_Operation_Code[2]),
    .CarryIn(n1_bit_alu_6_carryout), .Operation(ALU_Operation_Code[1:0]), .CarryOut(n1_bit_alu_7_carryout),
    .Result(Result[6]));  // open: Set
  _1_bit_ALU u_1_bit_alu_8 (
    .a(a[7]), .b(b[7]), .Less(1'b0), .Ainvert(ALU_Operation_Code[3]), .Binvert(ALU_Operation_Code[2]),
    .CarryIn(n1_bit_alu_7_carryout), .Operation(ALU_Operation_Code[1:0]), .CarryOut(n1_bit_alu_8_carryout),
    .Result(Result[7]));  // open: Set
  _1_bit_ALU u_1_bit_alu_9 (
    .a(a[8]), .b(b[8]), .Less(1'b0), .Ainvert(ALU_Operation_Code[3]), .Binvert(ALU_Operation_Code[2]),
    .CarryIn(n1_bit_alu_8_carryout), .Operation(ALU_Operation_Code[1:0]), .CarryOut(n1_bit_alu_9_carryout),
    .Result(Result[8]));  // open: Set
  _1_bit_ALU u_1_bit_alu_10 (
    .a(a[9]), .b(b[9]), .Less(1'b0), .Ainvert(ALU_Operation_Code[3]), .Binvert(ALU_Operation_Code[2]),
    .CarryIn(n1_bit_alu_9_carryout), .Operation(ALU_Operation_Code[1:0]), .CarryOut(n1_bit_alu_10_carryout),
    .Result(Result[9]));  // open: Set
  _1_bit_ALU u_1_bit_alu_11 (
    .a(a[10]), .b(b[10]), .Less(1'b0), .Ainvert(ALU_Operation_Code[3]), .Binvert(ALU_Operation_Code[2]),
    .CarryIn(n1_bit_alu_10_carryout), .Operation(ALU_Operation_Code[1:0]), .CarryOut(n1_bit_alu_11_carryout),
    .Result(Result[10]));  // open: Set
  _1_bit_ALU u_1_bit_alu_12 (
    .a(a[11]), .b(b[11]), .Less(1'b0), .Ainvert(ALU_Operation_Code[3]), .Binvert(ALU_Operation_Code[2]),
    .CarryIn(n1_bit_alu_11_carryout), .Operation(ALU_Operation_Code[1:0]), .CarryOut(n1_bit_alu_12_carryout),
    .Result(Result[11]));  // open: Set
  _1_bit_ALU u_1_bit_alu_13 (
    .a(a[12]), .b(b[12]), .Less(1'b0), .Ainvert(ALU_Operation_Code[3]), .Binvert(ALU_Operation_Code[2]),
    .CarryIn(n1_bit_alu_12_carryout), .Operation(ALU_Operation_Code[1:0]), .CarryOut(n1_bit_alu_13_carryout),
    .Result(Result[12]));  // open: Set
  _1_bit_ALU u_1_bit_alu_14 (
    .a(a[13]), .b(b[13]), .Less(1'b0), .Ainvert(ALU_Operation_Code[3]), .Binvert(ALU_Operation_Code[2]),
    .CarryIn(n1_bit_alu_13_carryout), .Operation(ALU_Operation_Code[1:0]), .CarryOut(n1_bit_alu_14_carryout),
    .Result(Result[13]));  // open: Set
  _1_bit_ALU u_1_bit_alu_15 (
    .a(a[14]), .b(b[14]), .Less(1'b0), .Ainvert(ALU_Operation_Code[3]), .Binvert(ALU_Operation_Code[2]),
    .CarryIn(n1_bit_alu_14_carryout), .Operation(ALU_Operation_Code[1:0]), .CarryOut(n1_bit_alu_15_carryout),
    .Result(Result[14]));  // open: Set
  _1_bit_ALU u_1_bit_alu_16 (
    .a(a[15]), .b(b[15]), .Less(1'b0), .Ainvert(ALU_Operation_Code[3]), .Binvert(ALU_Operation_Code[2]),
    .CarryIn(n1_bit_alu_15_carryout), .Operation(ALU_Operation_Code[1:0]), .CarryOut(n1_bit_alu_16_carryout),
    .Result(Result[15]));  // open: Set
  _1_bit_ALU u_1_bit_alu_17 (
    .a(a[16]), .b(b[16]), .Less(1'b0), .Ainvert(ALU_Operation_Code[3]), .Binvert(ALU_Operation_Code[2]),
    .CarryIn(n1_bit_alu_16_carryout), .Operation(ALU_Operation_Code[1:0]), .CarryOut(n1_bit_alu_17_carryout),
    .Result(Result[16]));  // open: Set
  _1_bit_ALU u_1_bit_alu_18 (
    .a(a[17]), .b(b[17]), .Less(1'b0), .Ainvert(ALU_Operation_Code[3]), .Binvert(ALU_Operation_Code[2]),
    .CarryIn(n1_bit_alu_17_carryout), .Operation(ALU_Operation_Code[1:0]), .CarryOut(n1_bit_alu_18_carryout),
    .Result(Result[17]));  // open: Set
  _1_bit_ALU u_1_bit_alu_19 (
    .a(a[18]), .b(b[18]), .Less(1'b0), .Ainvert(ALU_Operation_Code[3]), .Binvert(ALU_Operation_Code[2]),
    .CarryIn(n1_bit_alu_18_carryout), .Operation(ALU_Operation_Code[1:0]), .CarryOut(n1_bit_alu_19_carryout),
    .Result(Result[18]));  // open: Set
  _1_bit_ALU u_1_bit_alu_20 (
    .a(a[19]), .b(b[19]), .Less(1'b0), .Ainvert(ALU_Operation_Code[3]), .Binvert(ALU_Operation_Code[2]),
    .CarryIn(n1_bit_alu_19_carryout), .Operation(ALU_Operation_Code[1:0]), .CarryOut(n1_bit_alu_20_carryout),
    .Result(Result[19]));  // open: Set
  _1_bit_ALU u_1_bit_alu_21 (
    .a(a[20]), .b(b[20]), .Less(1'b0), .Ainvert(ALU_Operation_Code[3]), .Binvert(ALU_Operation_Code[2]),
    .CarryIn(n1_bit_alu_20_carryout), .Operation(ALU_Operation_Code[1:0]), .CarryOut(n1_bit_alu_21_carryout),
    .Result(Result[20]));  // open: Set
  _1_bit_ALU u_1_bit_alu_22 (
    .a(a[21]), .b(b[21]), .Less(1'b0), .Ainvert(ALU_Operation_Code[3]), .Binvert(ALU_Operation_Code[2]),
    .CarryIn(n1_bit_alu_21_carryout), .Operation(ALU_Operation_Code[1:0]), .CarryOut(n1_bit_alu_22_carryout),
    .Result(Result[21]));  // open: Set
  _1_bit_ALU u_1_bit_alu_23 (
    .a(a[22]), .b(b[22]), .Less(1'b0), .Ainvert(ALU_Operation_Code[3]), .Binvert(ALU_Operation_Code[2]),
    .CarryIn(n1_bit_alu_22_carryout), .Operation(ALU_Operation_Code[1:0]), .CarryOut(n1_bit_alu_23_carryout),
    .Result(Result[22]));  // open: Set
  _1_bit_ALU u_1_bit_alu_24 (
    .a(a[23]), .b(b[23]), .Less(1'b0), .Ainvert(ALU_Operation_Code[3]), .Binvert(ALU_Operation_Code[2]),
    .CarryIn(n1_bit_alu_23_carryout), .Operation(ALU_Operation_Code[1:0]), .CarryOut(n1_bit_alu_24_carryout),
    .Result(Result[23]));  // open: Set
  _1_bit_ALU u_1_bit_alu_25 (
    .a(a[24]), .b(b[24]), .Less(1'b0), .Ainvert(ALU_Operation_Code[3]), .Binvert(ALU_Operation_Code[2]),
    .CarryIn(n1_bit_alu_24_carryout), .Operation(ALU_Operation_Code[1:0]), .CarryOut(n1_bit_alu_25_carryout),
    .Result(Result[24]));  // open: Set
  _1_bit_ALU u_1_bit_alu_26 (
    .a(a[25]), .b(b[25]), .Less(1'b0), .Ainvert(ALU_Operation_Code[3]), .Binvert(ALU_Operation_Code[2]),
    .CarryIn(n1_bit_alu_25_carryout), .Operation(ALU_Operation_Code[1:0]), .CarryOut(n1_bit_alu_26_carryout),
    .Result(Result[25]));  // open: Set
  _1_bit_ALU u_1_bit_alu_27 (
    .a(a[26]), .b(b[26]), .Less(1'b0), .Ainvert(ALU_Operation_Code[3]), .Binvert(ALU_Operation_Code[2]),
    .CarryIn(n1_bit_alu_26_carryout), .Operation(ALU_Operation_Code[1:0]), .CarryOut(n1_bit_alu_27_carryout),
    .Result(Result[26]));  // open: Set
  _1_bit_ALU u_1_bit_alu_28 (
    .a(a[27]), .b(b[27]), .Less(1'b0), .Ainvert(ALU_Operation_Code[3]), .Binvert(ALU_Operation_Code[2]),
    .CarryIn(n1_bit_alu_27_carryout), .Operation(ALU_Operation_Code[1:0]), .CarryOut(n1_bit_alu_28_carryout),
    .Result(Result[27]));  // open: Set
  _1_bit_ALU u_1_bit_alu_29 (
    .a(a[28]), .b(b[28]), .Less(1'b0), .Ainvert(ALU_Operation_Code[3]), .Binvert(ALU_Operation_Code[2]),
    .CarryIn(n1_bit_alu_28_carryout), .Operation(ALU_Operation_Code[1:0]), .CarryOut(n1_bit_alu_29_carryout),
    .Result(Result[28]));  // open: Set
  _1_bit_ALU u_1_bit_alu_30 (
    .a(a[29]), .b(b[29]), .Less(1'b0), .Ainvert(ALU_Operation_Code[3]), .Binvert(ALU_Operation_Code[2]),
    .CarryIn(n1_bit_alu_29_carryout), .Operation(ALU_Operation_Code[1:0]), .CarryOut(n1_bit_alu_30_carryout),
    .Result(Result[29]));  // open: Set
  _1_bit_ALU u_1_bit_alu_31 (
    .a(a[30]), .b(b[30]), .Less(1'b0), .Ainvert(ALU_Operation_Code[3]), .Binvert(ALU_Operation_Code[2]),
    .CarryIn(n1_bit_alu_30_carryout), .Operation(ALU_Operation_Code[1:0]), .CarryOut(n1_bit_alu_31_carryout),
    .Result(Result[30]));  // open: Set
  _1_bit_ALU u_1_bit_alu_32 (
    .a(a[31]), .b(b[31]), .Less(1'b0), .Ainvert(ALU_Operation_Code[3]), .Binvert(ALU_Operation_Code[2]),
    .CarryIn(n1_bit_alu_31_carryout), .Operation(ALU_Operation_Code[1:0]), .CarryOut(Overflow),
    .Result(Result[31]), .Set(n1_bit_alu_32_set));
  or or_1 (or_1_out, Result[0], Result[1], Result[2], Result[3], Result[4], Result[5], Result[6], Result[7]);
  or or_2 (or_2_out, Result[8], Result[9], Result[10], Result[11], Result[12], Result[13], Result[14], Result[15]);
  or or_3 (or_3_out, Result[16], Result[17], Result[18], Result[19], Result[20], Result[21], Result[22], Result[23]);
  or or_4 (or_4_out, Result[24], Result[25], Result[26], Result[27], Result[28], Result[29], Result[30], Result[31]);
  or or_5 (or_5_out, or_1_out, or_2_out, or_3_out, or_4_out);
  not not_1 (Zero, or_5_out);
endmodule
